// Logisim project wikiarduino.circ as structural Verilog: 2 circuits, main circuit main
module main (
  input  _9,
  input  _8,
  input  _7,
  input  _6,
  input  _5,
  input  _4,
  input  _3,
  input  in_8,
  input  in_9,
  input  in_10,
  input  in_11,
  input  in_12,
  input  in_13,
  output _2,
  output a0,
  output a1,
  output a2,
  output a3,
  output a4,
  output a5
);

  wire and_1_out, and_2_out, and_3_out, and_4_out, and_5_out, and_6_out, and_7_out, and_8_out,
       decoder_1_out0, decoder_1_out1, decoder_1_out2, decoder_1_out3, decoder_1_out4, decoder_1_out5,
       decoder_1_out6, decoder_1_out7, register_1_output, register_2_output, register_3_output,
       register_4_output, register_5_output, register_6_output, register_7_output, register_8_output;

  Decoder #(.select(3), .enable("false")) decoder_1 (
    .out0(decoder_1_out0), .out1(decoder_1_out1), .out2(decoder_1_out2), .out3(decoder_1_out3),
    .out4(decoder_1_out4), .out5(decoder_1_out5), .out6(decoder_1_out6), .out7(decoder_1_out7),
    .sel({_7, _6, _5}));
  and and_1 (and_1_out, decoder_1_out0, _3);
  and and_2 (and_2_out, decoder_1_out1, _3);
  and and_3 (and_3_out, decoder_1_out2, _3);
  and and_4 (and_4_out, decoder_1_out3, _3);
  and and_5 (and_5_out, decoder_1_out4, _3);
  and and_6 (and_6_out, decoder_1_out5, _3);
  and and_7 (and_7_out, decoder_1_out6, _3);
  and and_8 (and_8_out, decoder_1_out7, _3);
  register register_1 (.Data(_4), .Clock(and_1_out), .Output(register_1_output));  // open: out_4
  register register_2 (.Data(_4), .Clock(and_2_out), .Output(register_2_output));  // open: out_4
  register register_3 (.Data(_4), .Clock(and_3_out), .Output(register_3_output));  // open: out_4
  register register_4 (.Data(_4), .Clock(and_4_out), .Output(register_4_output));  // open: out_4
  register register_5 (.Data(_4), .Clock(and_5_out), .Output(register_5_output));  // open: out_4
  register register_6 (.Data(_4), .Clock(and_6_out), .Output(register_6_output));  // open: out_4
  register register_7 (.Data(_4), .Clock(and_7_out), .Output(register_7_output));  // open: out_4
  register register_8 (.Data(_4), .Clock(and_8_out), .Output(register_8_output));  // open: out_4
  Multiplexer #(.select(3), .enable("false")) multiplexer_1 (
    .in0(register_1_output), .in1(register_2_output), .in2(register_3_output), .in3(register_4_output),
    .in4(register_5_output), .in5(register_6_output), .in6(register_7_output), .in7(register_8_output),
    .out(_2), .sel({_7, _6, _5}));

  assign a0 = in_8;
  assign a1 = in_9;
  assign a2 = in_10;
  assign a3 = in_11;
  assign a4 = in_12;
  assign a5 = in_13;

  // Notes on the sheet:
  //   il numero sotto il pin è il numero del pin sulla board di arduino
  //   collegamento con i sensori ... il pin a0 gestisce unicamente il sensore di temperatura
  //   quindi contiene al suo interno già la conversione in temperatura
  //   gli altri pin invece restituiscono semplicemente il valore grezzo
endmodule

module register (
  input  Data,
  input  Clock,
  output Output,
  output out_4
);

  wire and_1_out, and_2_out, not_1_out;

  not not_1 (not_1_out, Data);
  and and_1 (and_1_out, not_1_out, Clock);
  and and_2 (and_2_out, Clock, Data);
  nor nor_1 (Output, and_1_out, out_4);
  nor nor_2 (out_4, Output, and_2_out);
endmodule
