# Fritzing sketch wikiarduino (saved by Fritzing 0.9.3b)
circuit board: 8.46667cm x 5.64444cm
breadboards: 1

parts:
  Part1 = Arduino Ethernet Shield (Rev3)
  LED1 = LED - 5mm [color="Red (633nm)" package="5 mm [THT]"]
  LED2 = LED - 5mm [color="Red (633nm)" package="5 mm [THT]"]
  LED3 = LED - 5mm [color="Red (633nm)" package="5 mm [THT]"]
  LED4 = LED - 5mm [color="Red (633nm)" package="5 mm [THT]"]
  LED5 = LED - 5mm [color="Red (633nm)" package="5 mm [THT]"]
  LED6 = LED - 5mm [color="Red (633nm)" package="5 mm [THT]"]
  LED7 = LED - 5mm [color="Red (633nm)" package="5 mm [THT]"]
  LED8 = LED - 5mm [color="Red (633nm)" package="5 mm [THT]"]
  U1 = TMP36 [package=to-92-kit]

nets:
  N1: Part1.D8, LED7.anode
  N2: Part1.PWM_D9, LED8.anode
  GND: Part1.GND, LED1.cathode, LED2.cathode, LED3.cathode, LED4.cathode, LED5.cathode, LED6.cathode, LED7.cathode, LED8.cathode, U1.GND
  N3: Part1.A0, U1.VOUT
  N4: Part1.D2, LED6.anode
  N5: Part1.PWM_D3, LED5.anode
  N6: Part1.SDCS, LED4.anode
  N7: Part1.PWM_D5, LED3.anode
  N8: Part1.PWM_D6, LED2.anode
  N9: Part1.D7, LED1.anode
  5V: Part1.5V, U1.VCC
